// Logisim project 4BitCPU.circ as structural Verilog: 5 circuits, main circuit main
module main (
  input  [3:0] in_1,
  input  in_2,
  input  in_3
);

  wire and_1_out, clock_1_out, decoder_1_out0, decoder_1_out1, decoder_1_out2, decoder_1_out3,
       decoder_1_out4, decoder_1_out5, decoder_1_out6, decoder_1_out7, decoder_1_out8, not_1_out, or_1_out,
       or_2_out, or_3_out, or_4_out, or_5_out;
  wire [3:0] alu_1_out_7, controlled_buffer_1_out, ram_1_dout, register_1_q, register_2_q, rom_1_data;
  wire [7:0] counter_1_q;

  Counter counter_1 (
    .count(and_1_out), .Q(counter_1_q), .up(1'b1), .clk(and_1_out), .clr(in_2));  // open: load, D, carry
  Clock clock_1 (.out(clock_1_out));
  not not_1 (not_1_out, in_3);
  ROM #(.dataWidth(4)) rom_1 (.addr(counter_1_q), .data(rom_1_data));
  and and_1 (and_1_out, not_1_out, clock_1_out);
  Decoder #(.enable("false"), .select(4)) decoder_1 (
    .out0(decoder_1_out0), .out1(decoder_1_out1), .out2(decoder_1_out2), .out3(decoder_1_out3),
    .out4(decoder_1_out4), .out5(decoder_1_out5), .out6(decoder_1_out6), .out7(decoder_1_out7),
    .out8(decoder_1_out8), .sel(rom_1_data));  // open: out9, out10, out11, out12, out13, out14, out15
  or or_1 (or_1_out, decoder_1_out8, decoder_1_out7, decoder_1_out6, decoder_1_out5);
  or or_2 (or_2_out, or_1_out, decoder_1_out2);
  Register #(.width(4)) register_1 (.D(alu_1_out_7), .en(or_2_out), .clk(and_1_out), .Q(register_1_q));  // open: clr
  Register #(.width(4)) register_2 (
    .D(alu_1_out_7), .en(decoder_1_out4), .clk(and_1_out), .Q(register_2_q));  // open: clr
  Hex_Digit_Display BVal (.value(register_2_q));  // open: dp
  or or_3 (or_3_out, decoder_1_out1, decoder_1_out3);
  or or_4 (or_4_out, decoder_1_out2, decoder_1_out4);
  assign controlled_buffer_1_out = decoder_1_out1 ? register_1_q : 4'bz;  // Controlled_Buffer controlled_buffer_1
  assign controlled_buffer_1_out = decoder_1_out3 ? register_2_q : 4'bz;  // Controlled_Buffer controlled_buffer_2
  Hex_Digit_Display AVal (.value(register_1_q));  // open: dp
  RAM #(.addrWidth(4), .dataWidth(4)) ram_1 (
    .addr(in_1), .we(or_3_out), .oe(or_4_out), .clk(and_1_out), .din(controlled_buffer_1_out),
    .dout(ram_1_dout));
  ALU alu_1 (
    .A(register_1_q), .B(register_2_q), .CLR(decoder_1_out5), .ADD(decoder_1_out6), .SUB(decoder_1_out7),
    .CMP(decoder_1_out8), .out_7(alu_1_out_7));
  or or_5 (or_5_out, decoder_1_out4, decoder_1_out2);
  assign alu_1_out_7 = or_5_out ? ram_1_dout : 4'bz;  // Controlled_Buffer controlled_buffer_3
  Hex_Digit_Display BusVal (.value(alu_1_out_7));  // open: dp
  Hex_Digit_Display hex_digit_display_1 (.value(ram_1_dout));  // open: dp

  // Notes on the sheet:
  //   contents of rom_1 (hex, n*v repeats v):
  //   4 6 1
  //   BVal
endmodule

module reg4 (
  input  [3:0] DataIn,
  input  RegIn,
  input  Clock,
  output [3:0] out_4
);

  Register #(.width(1)) register_1 (.D(DataIn[0]), .en(RegIn), .clk(Clock), .Q(out_4[0]));  // open: clr
  Register #(.width(1)) register_2 (.D(DataIn[1]), .en(RegIn), .clk(Clock), .Q(out_4[1]));  // open: clr
  Register #(.width(1)) register_3 (.D(DataIn[2]), .en(RegIn), .clk(Clock), .Q(out_4[2]));  // open: clr
  Register #(.width(1)) register_4 (.D(DataIn[3]), .en(RegIn), .clk(Clock), .Q(out_4[3]));  // open: clr
endmodule

module ALU (
  input  [3:0] A,
  input  [3:0] B,
  input  CLR,
  input  ADD,
  input  SUB,
  input  CMP,
  output [3:0] out_7
);

  wire [1:0] decoder2_1_out_5;
  wire [3:0] adder_1_out, cmp4_1_out_4, subtractor_1_out;

  Hex_Digit_Display hex_digit_display_1 (.value(A));  // open: dp
  Hex_Digit_Display hex_digit_display_2 (.value(B));  // open: dp
  Adder #(.width(4)) adder_1 (.a(A), .b(B), .out(adder_1_out));  // open: cin, cout
  Subtractor #(.width(4)) subtractor_1 (.a(A), .b(B), .out(subtractor_1_out));  // open: bin, bout
  Hex_Digit_Display hex_digit_display_3 (.value(adder_1_out));  // open: dp
  Decoder2 decoder2_1 (.in_1(CLR), .in_2(ADD), .in_3(SUB), .in_4(CMP), .out_5(decoder2_1_out_5));
  CMP4 cmp4_1 (.in_1(A), .in_2(B), .out_4(cmp4_1_out_4));  // open: in_3
  Hex_Digit_Display hex_digit_display_4 (.value(subtractor_1_out));  // open: dp
  Multiplexer #(.select(2), .width(4)) multiplexer_1 (
    .in1(adder_1_out), .in2(subtractor_1_out), .in3(cmp4_1_out_4), .out(out_7), .sel(decoder2_1_out_5));  // open: in0
  Hex_Digit_Display hex_digit_display_5 (.value(out_7));  // open: dp

  // Notes on the sheet:
  //   CMP
endmodule

module CMP4 (
  input  [3:0] in_1,
  input  [3:0] in_2,
  input  in_3,
  output [3:0] out_4
);

  Comparator #(.mode("unsigned"), .width(4)) comparator_1 (
    .a(in_1), .b(in_2), .gt(out_4[0]), .eq(out_4[1]), .lt(out_4[2]));

  assign out_4[3] = in_3;
endmodule

module Decoder2 (
  input  in_1,
  input  in_2,
  input  in_3,
  input  in_4,
  output [1:0] out_5
);

  or or_1 (out_5[0], in_2, in_4);
  or or_2 (out_5[1], in_3, in_4);

  // Notes on the sheet:
  //   00 01 10 11
endmodule
